// Logisim project procesor.circ as structural Verilog
module Procesor (
  input  [7:0] Adress,
  input  [7:0] in_2,
  input  LD,
  input  [7:0] D,
  input  [7:0] S,
  input  [3:0] in_6,
  output [7:0] out_7,
  output [7:0] out_8,
  output [7:0] out_9,
  output out_10
);

  wire clock_1_out, clock_2_out, or_1_out;

  Clock clock_1 (.out(clock_1_out));
  RAM #(.bus("separate")) ram_1 (
    .addr(Adress), .din(in_2), .data(out_7), .clk(clock_1_out), .ld(LD));  // open: str, sel, clr
  ALU alu_1 (.X(D), .Y(S), .Z(out_8), .O(out_10), .in_3(in_6));
  or or_1 (or_1_out, in_6[0], in_6[1], in_6[2], in_6[3]);
  Clock clock_2 (.out(clock_2_out));
  // Registers registers_1: pin names not known; wires that end beside it: out_8, S[2:0], D[2:0], clock_2_out, or_1_out, out_9

  // Notes on the sheet:
  //   S
  //   D
endmodule
